# Fritzing sketch SENSORE PARCHEGGIO (saved by Fritzing 0.9.3b)
breadboards: 1

parts:
  Componente1 = SRF05 Ultrasonic Rangefinder
  LCM1602_IIC1 = LCM1602 IIC [part_number="LCM1602 IIC" chip_label="LCM1602 IIC" package="DIP (Dual Inline) [THT]"]
  LCD1 = LCD screen  # not connected
  Componente2 = Arduino Uno (Rev3)
  J1 = Piezo Speaker

nets:
  VCC: Componente1.VCC, Componente2.5V
  N1: Componente1.Trig, Componente2.D7
  N2: Componente1.Echo, Componente2.D8
  GND: Componente1.GND, Componente2.GND, J1.pin1
  N3: LCM1602_IIC1.SDA, Componente2.A4/SDA
  N4: LCM1602_IIC1.SCL, Componente2.A5/SCL
  N5: Componente2.D9_PWM, J1.pin2

custom parts:
  LCM1602 IIC: I2C-Module to use a 1602 or 2004 LCD on with the wire.h libory Serial LCD Modul
